# Fritzing sketch GamesCase2Servos (saved by Fritzing 0.7.11b)
breadboards: 1

parts:
  U1 = atmega328 [package=dip]
  C4 = Ceramic Capacitor [capacitance=100nF package="200 mil [THT, multilayer]"]
  C5 = Ceramic Capacitor [capacitance=22µF package="200 mil [THT, multilayer]"]
  C6 = Ceramic Capacitor [capacitance=22µF package="200 mil [THT, multilayer]"]
  R1 = 10k Ω Resistor [package=THT]
  XTAL1 = Crystal [frequency="16 Mhz" package=THT]
  J1 = double row male pin header, 2 pins [form="♂ (male)"]  # not connected
  J3 = double row male pin header, 2 pins [form="♂ (male)"]
  J4 = Basic Servo
  LED1 = LED - 3mm [color="Red (633nm)" package="3 mm [THT]"]
  R4 = Rotary Potentiometer (Large) [maximum_resistance=100kΩ package=THT]
  R10 = Resistor [tolerance=±5% resistance=470 package=THT]
  J6 = female pin header, 2 pins [form="♀ (female)"]
  J7 = female pin header, 3 pins [form="♀ (female)"]
  J8 = female pin header, 3 pins [form="♀ (female)"]
  J9 = Basic Servo
  J10 = female pin header, 3 pins [form="♀ (female)"]

nets:
  N1: U1.RESET, U1.D0_(RX), C4.1, R1.Pin_0, J3.pin2
  N2: U1.D1_(TX), J3.pin1
  VCC: U1.D4, U1.VCC, U1.AVCC, R1.Pin_1, J4.vcc, R4.leg2, R10.Pin_0, J7.pin3, J8.pin2, J9.vcc, J10.pin2
  GND: U1.GND, C5.0, C6.0, J4.gnd, LED1.cathode, R4.leg1, J6.pin2, J7.pin1, J8.pin3, J9.gnd, J10.pin1
  N3: U1.XLAT1, C6.1, XTAL1.pin_1
  N4: U1.XLAT2, C5.1, XTAL1.pin_0
  N5: U1.D10_(PWM), J4.pulse, J8.pin1
  N6: U1.D11_(PWM), J9.pulse, J10.pin3
  N7: U1.A5, R4.wiper, J7.pin2
  N8: LED1.anode, R10.Pin_1, J6.pin1
