# Fritzing sketch connor-disco-light-long (saved by Fritzing 0.7.11b)
breadboards: 3

parts:
  U1 = atmega328 [package=dip]
  C4 = Ceramic Capacitor [capacitance=100nF package="200 mil [THT, multilayer]"]
  C5 = Ceramic Capacitor [capacitance=22µF package="200 mil [THT, multilayer]"]
  C6 = Ceramic Capacitor [capacitance=22µF package="200 mil [THT, multilayer]"]
  R1 = 10k Ω Resistor [package=THT]
  XTAL1 = Crystal [frequency="16 Mhz" package=THT]
  J1 = double row male pin header, 2 pins [form="♂ (male)"]
  J3 = double row male pin header, 2 pins [form="♂ (male)"]
  J4 = Piezo Speaker
  J5 = Basic Servo
  J6 = Basic Servo
  S1 = Toggle Switch [package=THT]  # not connected
  R2 = 1M Ω Resistor [package=THT]
  U6 = 74HC595 [package="DIP16 [THT]"]
  U7 = 74HC595 [package="DIP16 [THT]"]
  U8 = 74HC595 [package="DIP16 [THT]"]
  J8 = male pin header, 12 pins [form="♂ (male)"]
  R3 = 1M Ω Resistor [package=THT]
  R4 = 1M Ω Resistor [package=THT]
  R5 = 1M Ω Resistor [package=THT]
  R6 = 1M Ω Resistor [package=THT]
  R7 = 1M Ω Resistor [package=THT]
  R8 = 1M Ω Resistor [package=THT]
  R9 = 1M Ω Resistor [package=THT]
  R10 = 1M Ω Resistor [package=THT]
  R11 = 1M Ω Resistor [package=THT]
  R12 = 1M Ω Resistor [package=THT]
  R13 = 1M Ω Resistor [package=THT]
  R14 = 1M Ω Resistor [package=THT]
  R15 = 1M Ω Resistor [package=THT]
  R16 = 1M Ω Resistor [package=THT]
  R17 = 1M Ω Resistor [package=THT]
  J9 = male pin header, 12 pins [form="♂ (male)"]
  C7 = Ceramic Capacitor [capacitance=1µF package="100 mil [THT, multilayer]"]
  R18 = Resistor [tolerance=±5% resistance=220 package=THT]

nets:
  N1: U1.RESET, U1.D0_(RX), C4.1, R1.Pin_0, J3.pin2
  N2: U1.D1_(TX), J3.pin1
  VCC: U1.D4, U1.VCC, U1.AVCC, R1.Pin_1, J1.pin1, J5.vcc, J6.vcc, U6.MR, U6.VCC, U7.MR, U7.VCC
  GND: U1.GND, C5.0, C6.0, J4.pin1, J5.gnd, J6.gnd, U6.GND, U6.OE, U7.GND, U7.OE, U8.GND, C7.1, R18.Pin_1
  N3: U1.XLAT1, C6.1, XTAL1.pin_1
  N4: U1.XLAT2, C5.1, XTAL1.pin_0
  N5: U1.D5_(PWM), J6.pulse
  N6: U1.D6_(PWM), J5.pulse
  N7: U1.D9_(PWM), U6.ST_CP, U7.ST_CP, C7.0
  N8: U1.D10_(PWM), U6.SH_CP, U7.SH_CP
  N9: U1.D11_(PWM), U7.DS
  N10: U1.D13, U6.DS
  N11: U1.A5, R18.Pin_0
  N12: R2.Pin_0, J8.pin2
  N13: R2.Pin_1, U6.Q7
  N14: U6.Q1, R8.Pin_1
  N15: U6.Q2, R7.Pin_1
  N16: U6.Q3, R6.Pin_1
  N17: U6.Q4, R5.Pin_1
  N18: U6.Q5, R4.Pin_1
  N19: U6.Q6, R3.Pin_1
  N20: U6.Q0, R9.Pin_1
  N21: U7.Q1, R12.Pin_1
  N22: U7.Q2, R16.Pin_1
  N23: U7.Q3, R17.Pin_1
  N24: U7.Q4, R14.Pin_1
  N25: U7.Q5, R13.Pin_1
  N26: U7.Q6, R11.Pin_1
  N27: U7.Q7, R10.Pin_1
  N28: U7.Q0, R15.Pin_1
  N29: U8.Q1, J9.pin7
  N30: U8.Q2, J9.pin4
  N31: U8.Q3, J9.pin1
  N32: U8.Q4, J8.pin10
  N33: U8.Q5, J8.pin7
  N34: U8.Q6, J8.pin4
  N35: U8.Q7, J8.pin1
  N36: J8.pin3, R10.Pin_0
  N37: J8.pin5, R3.Pin_0
  N38: J8.pin6, R11.Pin_0
  N39: J8.pin8, R4.Pin_0
  N40: J8.pin9, R13.Pin_0
  N41: J8.pin11, R5.Pin_0
  N42: J8.pin12, R14.Pin_0
  N43: R6.Pin_0, J9.pin2
  N44: R7.Pin_0, J9.pin5
  N45: R8.Pin_0, J9.pin8
  N46: R9.Pin_0, J9.pin11
  N47: R12.Pin_0, J9.pin9
  N48: R15.Pin_0, J9.pin12
  N49: R16.Pin_0, J9.pin6
  N50: R17.Pin_0, J9.pin3
