# Fritzing sketch connor-disco-light-wide (saved by Fritzing 0.7.11b)
breadboards: 2

parts:
  U1 = atmega328 [package=dip]
  C4 = Ceramic Capacitor [capacitance=100nF package="200 mil [THT, multilayer]"]
  C5 = Ceramic Capacitor [capacitance=22µF package="200 mil [THT, multilayer]"]
  C6 = Ceramic Capacitor [capacitance=22µF package="200 mil [THT, multilayer]"]
  R1 = 10k Ω Resistor [package=THT]
  XTAL1 = Crystal [frequency="16 Mhz" package=THT]
  J1 = double row male pin header, 2 pins [form="♂ (male)"]
  J3 = double row male pin header, 2 pins [form="♂ (male)"]
  J4 = Piezo Speaker
  J5 = Basic Servo
  J6 = Basic Servo
  S1 = Toggle Switch [package=THT]  # not connected
  R2 = 1M Ω Resistor [package=THT]  # not connected
  U6 = 74HC595 [package="DIP16 [THT]"]  # not connected
  U7 = 74HC595 [package="DIP16 [THT]"]  # not connected
  U8 = 74HC595 [package="DIP16 [THT]"]
  J7 = male pin header, 12 pins [form="♂ (male)"]
  J8 = male pin header, 12 pins [form="♂ (male)"]

nets:
  N1: U1.RESET, U1.D0_(RX), C4.1, R1.Pin_0, J3.pin2
  N2: U1.D1_(TX), J3.pin1
  VCC: U1.D4, U1.VCC, U1.AVCC, R1.Pin_1, J1.pin1, J5.vcc, J6.vcc
  GND: U1.GND, C5.0, C6.0, J4.pin1, J5.gnd, J6.gnd
  N3: U1.XLAT1, C6.1, XTAL1.pin_1
  N4: U1.XLAT2, C5.1, XTAL1.pin_0
  N5: U1.D5_(PWM), J6.pulse
  N6: U1.D6_(PWM), J5.pulse
  N7: U1.D12, U8.DS
  N8: U8.Q1, J8.pin8
  N9: U8.Q2, J8.pin5
  N10: U8.Q3, J8.pin2
  N11: U8.Q4, J7.pin11
  N12: U8.Q5, J7.pin8
  N13: U8.Q6, J7.pin5
  N14: U8.Q7, J7.pin2
  N15: U8.Q0, J8.pin11

notes:
  Missed the resistors out :{
