# Fritzing sketch safe (saved by Fritzing 0.7.11b)
breadboards: 1

parts:
  U1 = atmega328 [package=dip]
  C4 = Ceramic Capacitor [capacitance=100nF package="200 mil [THT, multilayer]"]
  C5 = Ceramic Capacitor [capacitance=22µF package="200 mil [THT, multilayer]"]
  C6 = Ceramic Capacitor [capacitance=22µF package="200 mil [THT, multilayer]"]
  R1 = 10k Ω Resistor [package=THT]
  XTAL1 = Crystal [frequency="16 Mhz" package=THT]
  J1 = double row male pin header, 2 pins [form="♂ (male)"]  # not connected
  J3 = double row male pin header, 2 pins [form="♂ (male)"]
  U2 = Mystery Part - 7 pins [package=THT]
  R3 = Resistor [tolerance=±5% resistance=10k package=THT]
  LED1 = green smd LED [package="1206 [SMD]"]
  J4 = Basic Servo
  R5 = Resistor [tolerance=±5% resistance=220 package=THT]
  LED2 = red smd LED [package="1206 [SMD]"]
  R6 = Resistor [tolerance=±5% resistance=220 package=THT]
  J5 = female pin header, 7 pins [form="♀ (female)"]
  R7 = Resistor [tolerance=±5% resistance=10k package=THT]
  R8 = Resistor [tolerance=±5% resistance=10k package=THT]
  J6 = female pin header, 2 pins [form="♀ (female)"]
  J7 = female pin header, 2 pins [form="♀ (female)"]
  J8 = female pin header, 3 pins [form="♀ (female)"]

nets:
  N1: U1.RESET, U1.D0_(RX), C4.1, R1.Pin_0, J3.pin2
  N2: U1.D1_(TX), J3.pin1
  N3: U1.D2, R5.Pin_1
  N4: U1.D3_(PWM), R6.Pin_1
  VCC: U1.D4, U1.VCC, U1.AVCC, R1.Pin_1, J4.vcc, J8.pin2
  N5: U1.GND, C5.0, C6.0, R3.Pin_0, R7.Pin_0, R8.Pin_0
  N6: U1.XLAT1, C6.1, XTAL1.pin_1
  N7: U1.XLAT2, C5.1, XTAL1.pin_0
  N8: U1.D5_(PWM), J4.pulse, J8.pin3
  N9: U1.D6_(PWM), U2.leg5, R3.Pin_1, J5.pin5
  N10: U1.D7, U2.leg6, J5.pin6, R8.Pin_1
  N11: U1.D8, U2.leg7, J5.pin7, R7.Pin_1
  N12: U1.D9_(PWM), U2.leg4, J5.pin4
  N13: U1.D10_(PWM), U2.leg3, J5.pin3
  N14: U1.D11_(PWM), U2.leg2, J5.pin2
  N15: U1.D12, U2.leg1, J5.pin1
  N16: LED1.cathode, LED2.cathode, J6.pin2, J7.pin1
  N17: LED1.anode, R5.Pin_0, J6.pin1
  N18: J4.gnd, J8.pin1
  N19: LED2.anode, R6.Pin_0, J7.pin2
