# Fritzing sketch tom-trebuchet (saved by Fritzing 0.7.11b)
breadboards: 1

parts:
  U1 = atmega328 [package=dip]
  C4 = Ceramic Capacitor [capacitance=100nF package="200 mil [THT, multilayer]"]
  C5 = Ceramic Capacitor [capacitance=22µF package="200 mil [THT, multilayer]"]
  C6 = Ceramic Capacitor [capacitance=22µF package="200 mil [THT, multilayer]"]
  R1 = 10k Ω Resistor [package=THT]
  XTAL1 = Crystal [frequency="16 Mhz" package=THT]
  J1 = double row male pin header, 2 pins [form="♂ (male)"]  # not connected
  J3 = double row male pin header, 2 pins [form="♂ (male)"]
  J4 = Infrared Proximity Sensor
  R3 = Photocell (LDR) [package=THT]
  J5 = Basic Servo
  S1 = Pushbutton [package="[THT]"]
  LED1 = Blue smd LED [package="0603 [SMD]"]
  R4 = Resistor [tolerance=±5% resistance=10k package=THT]
  J6 = female pin header, 2 pins [form="♀ (female)"]
  J7 = female pin header, 2 pins [form="♀ (female)"]
  J8 = female pin header, 3 pins [form="♀ (female)"]
  J9 = female pin header, 3 pins [form="♀ (female)"]
  J10 = female pin header, 2 pins [form="♀ (female)"]
  R5 = Resistor [tolerance=±5% resistance=470 package=THT]
  R6 = Resistor [tolerance=±5% resistance=10k package=THT]

nets:
  N1: U1.RESET, U1.D0_(RX), C4.1, R1.Pin_0, J3.pin2
  N2: U1.D1_(TX), J3.pin1
  VCC: U1.D4, U1.VCC, U1.AVCC, R1.Pin_1, R3.pin_1, J5.vcc, J8.pin3, J9.pin2, J10.pin2
  GND: U1.GND, C5.0, C6.0, J4.GND, J5.gnd, LED1.cathode, J7.pin2, J8.pin2, J9.pin1, R5.Pin_0, R6.Pin_1
  N3: U1.XLAT1, C6.1, XTAL1.pin_1
  N4: U1.XLAT2, C5.1, XTAL1.pin_0
  N5: U1.D7, R5.Pin_1
  N6: U1.D8, S1.Pin_3, S1.Pin_4, R4.Pin_1, J6.pin1
  N7: U1.D9_(PWM), J5.pulse, J9.pin3
  N8: U1.A4, R3.pin_0, J10.pin1, R6.Pin_0
  N9: U1.A5, J4.Vout, J8.pin1
  N10: S1.Pin_1, S1.Pin_2, J6.pin2
  N11: LED1.anode, J7.pin1
